# Fritzing sketch enclosure (saved by Fritzing 0.9.4)
circuit board: 8.46667cm x 5.64444cm

parts:
  Part1 = Real Time Clock Module - DS1307 RTC Breakout Board
  MCU1 = Raspberry Pi Zero
  M1 = DC Motor
  Power_plug1 = Power plug
  Part2 = IFR520 MOS module [package=THT]
  S1 = Toggle Switch [package=THT]
  S2 = SWITCH-MOMENTARY-2 [package=tactile-pth-12mm]

nets:
  N1: Part1.5V, MCU1.pin_1, MCU1.pin_17
  N2: Part1.GND, MCU1.pin_3
  N3: Part1.SQW, MCU1.pin_5, MCU1.pin_11, S2.2
  N4: Part1.SCL, MCU1.pin_7
  GND: Part1.SDA, MCU1.pin_6, MCU1.pin_9, MCU1.pin_14, MCU1.pin_20, MCU1.pin_39, Power_plug1.GND, Part2.GND, S2.1
  N5: MCU1.pin_2, MCU1.pin_4, S1.COM
  N6: MCU1.pin_13, S1.L2
  N7: MCU1.pin_16, Part2.SIG
  N8: M1.pin_1, Part2.V+
  N9: M1.pin_2, Part2.V-
  VCC: Power_plug1.VCC, Part2.VIN
